// Logisim project 74164.circ as structural Verilog: 1 circuit, main circuit 74164
module _74164 (
  input  DSA,
  input  DSB,
  input  CP,
  input  nMR,
  output Q0,
  output Q1,
  output Q2,
  output Q3,
  output Q4,
  output Q5,
  output Q6,
  output Q7
);

  wire and_1_out, buffer_1_out, not_1_out;

  and and_1 (and_1_out, DSA, DSB);
  buf buffer_1 (buffer_1_out, CP);
  not not_1 (not_1_out, nMR);
  D_Flip_Flop d_ff_1 (.clk(buffer_1_out), .D(and_1_out), .Q(Q0), .reset(not_1_out));  // open: Qn, preset, en
  D_Flip_Flop d_ff_2 (.clk(buffer_1_out), .D(Q0), .Q(Q1), .reset(not_1_out));  // open: Qn, preset, en
  D_Flip_Flop d_ff_3 (.clk(buffer_1_out), .D(Q1), .Q(Q2), .reset(not_1_out));  // open: Qn, preset, en
  D_Flip_Flop d_ff_4 (.clk(buffer_1_out), .D(Q2), .Q(Q3), .reset(not_1_out));  // open: Qn, preset, en
  D_Flip_Flop d_ff_5 (.clk(buffer_1_out), .D(Q3), .Q(Q4), .reset(not_1_out));  // open: Qn, preset, en
  D_Flip_Flop d_ff_6 (.clk(buffer_1_out), .D(Q4), .Q(Q5), .reset(not_1_out));  // open: Qn, preset, en
  D_Flip_Flop d_ff_7 (.clk(buffer_1_out), .D(Q5), .Q(Q6), .reset(not_1_out));  // open: Qn, preset, en
  D_Flip_Flop d_ff_8 (.clk(buffer_1_out), .D(Q6), .Q(Q7), .reset(not_1_out));  // open: Qn, preset, en
endmodule
