// Logisim project test.circ as structural Verilog: 1 circuit, main circuit main
module main (
  input  reset,
  input  enable,
  output out_3,
  output out_4,
  output NOT_FOUND,
  output found
);

  wire and_1_out, and_2_out, and_3_out, and_4_out, and_5_out, and_6_out, and_7_out, and_9_out, CHECK_OR_out,
       clock_1_out, d_ff_1_q, d_ff_1_qn, d_ff_2_q, d_ff_3_q, d_ff_3_qn, not_1_out, not_2_out, not_3_out,
       not_4_out, not_5_out, not_6_out, or_1_out, shift_register_1_q0, shift_register_1_q2,
       shift_register_1_q3, xor_1_out, xor_2_out, xor_3_out, xor_4_out, xor_5_out, xor_6_out, xor_7_out,
       xor_8_out;

  Clock clock_1 (.out(clock_1_out));
  and and_1 (and_1_out, d_ff_3_q, d_ff_2_q);
  D_Flip_Flop d_ff_1 (
    .clk(clock_1_out), .D(and_1_out), .Q(d_ff_1_q), .Qn(d_ff_1_qn), .en(d_ff_1_qn), .reset(reset));  // open: preset
  xor xor_1 (xor_1_out, d_ff_3_q, d_ff_2_q);
  D_Flip_Flop d_ff_2 (
    .clk(clock_1_out), .D(xor_1_out), .Q(d_ff_2_q), .en(and_2_out), .reset(reset));  // open: Qn, preset
  and and_2 (and_2_out, enable, d_ff_1_qn, not_4_out);
  D_Flip_Flop d_ff_3 (
    .clk(clock_1_out), .D(d_ff_3_qn), .Q(d_ff_3_q), .Qn(d_ff_3_qn), .en(and_2_out), .reset(reset));  // open: preset
  ExactlyOne xor_2 (.out(xor_2_out), .in0(d_ff_2_q), .in2(d_ff_2_q), .in6(d_ff_3_q));
  xor xor_3 (xor_3_out, d_ff_2_q, d_ff_3_q);
  xor xor_4 (xor_4_out, d_ff_2_q, d_ff_3_q);
  Shift_Register #(.length(4)) shift_register_1 (
    .shift(d_ff_1_qn), .in(xor_2_out), .clk(clock_1_out), .clr(reset), .q0(shift_register_1_q0),
    .q2(shift_register_1_q2), .q3(shift_register_1_q3));  // open: out, load, d0, d1, q1, d2, d3
  xor xor_5 (xor_5_out, d_ff_2_q, d_ff_3_q);
  not not_1 (not_1_out, shift_register_1_q3);
  not not_2 (not_2_out, shift_register_1_q0);
  xor xor_6 (xor_6_out, xor_4_out, xor_5_out);
  xor xor_7 (xor_7_out, xor_3_out, xor_2_out);
  not not_3 (not_3_out, shift_register_1_q2);
  and CHECK_OR (CHECK_OR_out, shift_register_1_q2, shift_register_1_q0);
  and and_3 (and_3_out, not_1_out, not_2_out);
  xor xor_8 (xor_8_out, xor_6_out, xor_7_out);
  not not_4 (not_4_out, xor_8_out);
  or or_1 (or_1_out, and_3_out, not_3_out, CHECK_OR_out, shift_register_1_q3);
  and and_4 (and_4_out, CHECK_OR_out, d_ff_1_q);
  not not_5 (not_5_out, and_5_out);
  and and_5 (and_5_out, and_3_out, d_ff_1_q);
  and and_6 (and_6_out, shift_register_1_q3, d_ff_1_q);
  and and_7 (and_7_out, d_ff_1_q, not_6_out);
  not not_6 (not_6_out, or_1_out);
  and and_8 (found, not_4_out, d_ff_1_q, or_1_out);
  or or_2 (NOT_FOUND, xor_8_out, and_7_out);
  and and_9 (and_9_out, and_4_out, not_5_out);
  or or_3 (out_4, and_9_out, and_6_out);
  or or_4 (out_3, and_5_out, and_6_out);

  // Notes on the sheet:
  //   controler
  //   CHECK AND
  //   OR
  //    NAND
  //   AND
endmodule
