// Logisim project test1.circ as structural Verilog: 1 circuit, main circuit main
module main (
  input  reset,
  input  enable,
  output out_3,
  output out_4,
  output NOT_FOUND,
  output found
);

  wire and_1_out, and_2_out, and_3_out, and_4_out, and_5_out, and_7_out, CHECK_OR_out, clock_1_out,
       n7408_1_p2, n7408_1_p3, n7408_1_p8, n7408_1_p9, not_1_out, not_2_out, not_3_out, not_4_out, not_5_out,
       not_6_out, or_1_out, or_2_out, shift_register_1_q0, shift_register_1_q2, shift_register_1_q3,
       xor_1_out, xor_2_out, xor_3_out;
  wire [3:0] counter_1_q;

  Clock clock_1 (.out(clock_1_out));
  Counter #(.width(4), .max('hf)) counter_1 (
    .count(and_1_out), .Q(counter_1_q), .clk(clock_1_out), .clr(reset));  // open: load, D, carry
  and and_1 (and_1_out, enable, not_1_out, not_4_out);
  not not_1 (not_1_out, counter_1_q[2]);
  // _7408 7408_1: pin names not known; wires that end beside it: 1'b0, n7408_1_p2, n7408_1_p3, counter_1_q[1], counter_1_q[0], counter_1_q[0], counter_1_q[1], n7408_1_p8, n7408_1_p9, counter_1_q[0], counter_1_q[1], counter_1_q[1], counter_1_q[0], 1'b1
  xor xor_1 (xor_1_out, n7408_1_p9, n7408_1_p3);
  xor xor_2 (xor_2_out, n7408_1_p2, n7408_1_p8);
  xor xor_3 (xor_3_out, xor_1_out, xor_2_out);
  Shift_Register #(.length(4), .trigger("falling")) shift_register_1 (
    .shift(not_1_out), .in(n7408_1_p8), .clk(clock_1_out), .clr(reset), .q0(shift_register_1_q0),
    .q2(shift_register_1_q2), .q3(shift_register_1_q3));  // open: out, load, d0, d1, q1, d2, d3
  not not_2 (not_2_out, shift_register_1_q2);
  and CHECK_OR (CHECK_OR_out, shift_register_1_q2, shift_register_1_q0);
  or or_1 (or_1_out, shift_register_1_q3, shift_register_1_q0);
  not not_3 (not_3_out, or_1_out);
  not not_4 (not_4_out, xor_3_out);
  or or_2 (or_2_out, not_3_out, not_2_out, CHECK_OR_out, shift_register_1_q3);
  and and_2 (and_2_out, CHECK_OR_out, counter_1_q[2]);
  not not_5 (not_5_out, and_3_out);
  and and_3 (and_3_out, not_3_out, counter_1_q[2]);
  and and_4 (and_4_out, shift_register_1_q3, counter_1_q[2]);
  and and_5 (and_5_out, counter_1_q[2], not_6_out);
  not not_6 (not_6_out, or_2_out);
  and and_6 (found, not_4_out, counter_1_q[2], or_2_out);
  or or_3 (NOT_FOUND, xor_3_out, and_5_out);
  and and_7 (and_7_out, and_2_out, not_5_out);
  or or_4 (out_3, and_7_out, and_4_out);
  or or_5 (out_4, and_3_out, and_4_out);

  // Notes on the sheet:
  //   counter
  //   Qpar3
  //   Qpar3
  //   enable
  //   damaged
  //   enable for output
  //   check if IC working 
  //   shift regiser
  //   check XOR
  //   controler
  //   CHECK AND
  //   check NAND
  //   OR
  //    NAND
  //   AND
endmodule
